// Logisim project Mmaismais2.0.4-Exemplo02.circ as structural Verilog: 13 circuits, main circuit main
module main (
  input  [7:0] in_1
);

  wire _00, _01, _02, _03, _04, _05, _06, _07, _08, _09, _10, _11, _12, _13, _14, _15, _16, _17, _18, _19,
       _20, _21, _22, _23, _24, _25, _26, _27, _28, _29, _30, _31, _32, _33, _34, _35, _36, _37, _38, _39,
       _40, _41, _42, _43, _44, _45, _46, _47, _48, _49, _50, _52, _53, _54, _55, _56, _57, _58, _59, _60,
       _61, _62, _63;
  wire [7:0] m_1_out1, m_1_out2, m_1_out3;

  M m_1 (
    .In3(in_1), .Ativar_Clock(1'b1), .Out1(m_1_out1), .Out2(m_1_out2), .Out3(m_1_out3));  // open: In0, In1, In2, Out0
  D_Flip_Flop d_ff_1 (.clk(m_1_out2[0]), .D(m_1_out3[0]), .Q(_00));  // open: Qn, preset, en, reset
  D_Flip_Flop d_ff_2 (.clk(m_1_out2[0]), .D(m_1_out3[1]), .Q(_01));  // open: Qn, preset, en, reset
  D_Flip_Flop d_ff_3 (.clk(m_1_out2[0]), .D(m_1_out3[2]), .Q(_02));  // open: Qn, preset, en, reset
  D_Flip_Flop d_ff_4 (.clk(m_1_out2[0]), .D(m_1_out3[3]), .Q(_03));  // open: Qn, preset, en, reset
  D_Flip_Flop d_ff_5 (.clk(m_1_out2[0]), .D(m_1_out3[4]), .Q(_04));  // open: Qn, preset, en, reset
  D_Flip_Flop d_ff_6 (.clk(m_1_out2[0]), .D(m_1_out3[5]), .Q(_05));  // open: Qn, preset, en, reset
  D_Flip_Flop d_ff_7 (.clk(m_1_out2[0]), .D(m_1_out3[6]), .Q(_06));  // open: Qn, preset, en, reset
  D_Flip_Flop d_ff_8 (.clk(m_1_out2[0]), .D(m_1_out3[7]), .Q(_07));  // open: Qn, preset, en, reset
  D_Flip_Flop d_ff_9 (.clk(m_1_out2[0]), .D(_00), .Q(_08));  // open: Qn, preset, en, reset
  D_Flip_Flop d_ff_10 (.clk(m_1_out2[0]), .D(_01), .Q(_09));  // open: Qn, preset, en, reset
  D_Flip_Flop d_ff_11 (.clk(m_1_out2[0]), .D(_02), .Q(_10));  // open: Qn, preset, en, reset
  D_Flip_Flop d_ff_12 (.clk(m_1_out2[0]), .D(_03), .Q(_11));  // open: Qn, preset, en, reset
  D_Flip_Flop d_ff_13 (.clk(m_1_out2[0]), .D(_04), .Q(_12));  // open: Qn, preset, en, reset
  D_Flip_Flop d_ff_14 (.clk(m_1_out2[0]), .D(_05), .Q(_13));  // open: Qn, preset, en, reset
  D_Flip_Flop d_ff_15 (.clk(m_1_out2[0]), .D(_06), .Q(_14));  // open: Qn, preset, en, reset
  D_Flip_Flop d_ff_16 (.clk(m_1_out2[0]), .D(_07), .Q(_15));  // open: Qn, preset, en, reset
  LED led_1 (.in(_56));
  LED led_2 (.in(_48));
  LED led_3 (.in(_40));
  LED led_4 (.in(_57));
  LED led_5 (.in(_41));
  LED led_6 (.in(_49));
  LED led_7 (.in(_42));
  LED led_8 (.in(_50));
  LED led_9 (.in(_58));
  LED led_10 (.in(_43));
  LED led_11 (.in(_59));
  LED led_12 (.in(_43));
  LED led_13 (.in(_44));
  LED led_14 (.in(_52));
  LED led_15 (.in(_60));
  LED led_16 (.in(_61));
  LED led_17 (.in(_53));
  LED led_18 (.in(_45));
  LED led_19 (.in(_62));
  LED led_20 (.in(_46));
  LED led_21 (.in(_54));
  LED led_22 (.in(_55));
  LED led_23 (.in(_47));
  LED led_24 (.in(_63));
  D_Flip_Flop d_ff_17 (.clk(m_1_out2[0]), .D(_08), .Q(_16));  // open: Qn, preset, en, reset
  D_Flip_Flop d_ff_18 (.clk(m_1_out2[0]), .D(_09), .Q(_17));  // open: Qn, preset, en, reset
  D_Flip_Flop d_ff_19 (.clk(m_1_out2[0]), .D(_10), .Q(_18));  // open: Qn, preset, en, reset
  D_Flip_Flop d_ff_20 (.clk(m_1_out2[0]), .D(_11), .Q(_19));  // open: Qn, preset, en, reset
  D_Flip_Flop d_ff_21 (.clk(m_1_out2[0]), .D(_12), .Q(_20));  // open: Qn, preset, en, reset
  D_Flip_Flop d_ff_22 (.clk(m_1_out2[0]), .D(_13), .Q(_21));  // open: Qn, preset, en, reset
  D_Flip_Flop d_ff_23 (.clk(m_1_out2[0]), .D(_14), .Q(_22));  // open: Qn, preset, en, reset
  D_Flip_Flop d_ff_24 (.clk(m_1_out2[0]), .D(_15), .Q(_23));  // open: Qn, preset, en, reset
  LED led_25 (.in(_08));
  LED led_26 (.in(_24));
  LED led_27 (.in(_32));
  LED led_28 (.in(_16));
  LED led_29 (.in(_25));
  LED led_30 (.in(_17));
  LED led_31 (.in(_09));
  LED led_32 (.in(_33));
  LED led_33 (.in(_18));
  LED led_34 (.in(_10));
  LED led_35 (.in(_34));
  LED led_36 (.in(_26));
  LED led_37 (.in(_35));
  LED led_38 (.in(_19));
  LED led_39 (.in(_27));
  LED led_40 (.in(_11));
  LED led_41 (.in(_28));
  LED led_42 (.in(_12));
  LED led_43 (.in(_36));
  LED led_44 (.in(_20));
  LED led_45 (.in(_37));
  LED led_46 (.in(_29));
  LED led_47 (.in(_13));
  LED led_48 (.in(_21));
  LED led_49 (.in(_38));
  LED led_50 (.in(_22));
  LED led_51 (.in(_30));
  LED led_52 (.in(_14));
  LED led_53 (.in(_31));
  LED led_54 (.in(_15));
  LED led_55 (.in(_23));
  LED led_56 (.in(_39));
  LED led_57 (.in(_00));
  LED led_58 (.in(_01));
  LED led_59 (.in(_02));
  LED led_60 (.in(_03));
  LED led_61 (.in(_04));
  LED led_62 (.in(_05));
  LED led_63 (.in(_06));
  LED led_64 (.in(_07));
  LED led_65 ();  // open: in
  LED led_66 ();  // open: in
  LED led_67 ();  // open: in
  LED led_68 ();  // open: in
  LED led_69 ();  // open: in
  LED led_70 ();  // open: in
  LED led_71 ();  // open: in
  LED led_72 ();  // open: in
  D_Flip_Flop d_ff_25 (.clk(m_1_out2[0]), .D(_16), .Q(_24));  // open: Qn, preset, en, reset
  D_Flip_Flop d_ff_26 (.clk(m_1_out2[0]), .D(_17), .Q(_25));  // open: Qn, preset, en, reset
  D_Flip_Flop d_ff_27 (.clk(m_1_out2[0]), .D(_18), .Q(_26));  // open: Qn, preset, en, reset
  D_Flip_Flop d_ff_28 (.clk(m_1_out2[0]), .D(_19), .Q(_27));  // open: Qn, preset, en, reset
  D_Flip_Flop d_ff_29 (.clk(m_1_out2[0]), .D(_20), .Q(_28));  // open: Qn, preset, en, reset
  D_Flip_Flop d_ff_30 (.clk(m_1_out2[0]), .D(_21), .Q(_29));  // open: Qn, preset, en, reset
  D_Flip_Flop d_ff_31 (.clk(m_1_out2[0]), .D(_22), .Q(_30));  // open: Qn, preset, en, reset
  D_Flip_Flop d_ff_32 (.clk(m_1_out2[0]), .D(_23), .Q(_31));  // open: Qn, preset, en, reset
  LED led_73 ();  // open: in
  LED led_74 ();  // open: in
  LED led_75 ();  // open: in
  LED led_76 ();  // open: in
  LED led_77 ();  // open: in
  LED led_78 ();  // open: in
  LED led_79 ();  // open: in
  LED led_80 ();  // open: in
  LED led_81 ();  // open: in
  LED led_82 ();  // open: in
  LED led_83 ();  // open: in
  LED led_84 ();  // open: in
  LED led_85 ();  // open: in
  LED led_86 ();  // open: in
  LED led_87 ();  // open: in
  LED led_88 ();  // open: in
  D_Flip_Flop d_ff_33 (.clk(m_1_out2[0]), .D(_24), .Q(_32));  // open: Qn, preset, en, reset
  D_Flip_Flop d_ff_34 (.clk(m_1_out2[0]), .D(_25), .Q(_33));  // open: Qn, preset, en, reset
  D_Flip_Flop d_ff_35 (.clk(m_1_out2[0]), .D(_26), .Q(_34));  // open: Qn, preset, en, reset
  D_Flip_Flop d_ff_36 (.clk(m_1_out2[0]), .D(_27), .Q(_35));  // open: Qn, preset, en, reset
  D_Flip_Flop d_ff_37 (.clk(m_1_out2[0]), .D(_28), .Q(_36));  // open: Qn, preset, en, reset
  D_Flip_Flop d_ff_38 (.clk(m_1_out2[0]), .D(_29), .Q(_37));  // open: Qn, preset, en, reset
  D_Flip_Flop d_ff_39 (.clk(m_1_out2[0]), .D(_30), .Q(_38));  // open: Qn, preset, en, reset
  D_Flip_Flop d_ff_40 (.clk(m_1_out2[0]), .D(_31), .Q(_39));  // open: Qn, preset, en, reset
  LED led_89 ();  // open: in
  LED led_90 ();  // open: in
  LED led_91 ();  // open: in
  LED led_92 ();  // open: in
  LED led_93 ();  // open: in
  LED led_94 ();  // open: in
  LED led_95 ();  // open: in
  LED led_96 ();  // open: in
  LED led_97 ();  // open: in
  LED led_98 ();  // open: in
  LED led_99 ();  // open: in
  LED led_100 ();  // open: in
  LED led_101 ();  // open: in
  LED led_102 ();  // open: in
  LED led_103 ();  // open: in
  LED led_104 ();  // open: in
  LED led_105 ();  // open: in
  LED led_106 ();  // open: in
  LED led_107 ();  // open: in
  LED led_108 ();  // open: in
  LED led_109 ();  // open: in
  LED led_110 ();  // open: in
  LED led_111 ();  // open: in
  LED led_112 ();  // open: in
  LED led_113 ();  // open: in
  LED led_114 ();  // open: in
  LED led_115 ();  // open: in
  LED led_116 ();  // open: in
  LED led_117 ();  // open: in
  LED led_118 ();  // open: in
  LED led_119 ();  // open: in
  LED led_120 ();  // open: in
  LED led_121 ();  // open: in
  LED led_122 ();  // open: in
  LED led_123 ();  // open: in
  LED led_124 ();  // open: in
  LED led_125 ();  // open: in
  LED led_126 ();  // open: in
  LED led_127 ();  // open: in
  LED led_128 ();  // open: in
  D_Flip_Flop d_ff_41 (.clk(m_1_out2[0]), .D(_32), .Q(_40));  // open: Qn, preset, en, reset
  D_Flip_Flop d_ff_42 (.clk(m_1_out2[0]), .D(_33), .Q(_41));  // open: Qn, preset, en, reset
  D_Flip_Flop d_ff_43 (.clk(m_1_out2[0]), .D(_34), .Q(_42));  // open: Qn, preset, en, reset
  D_Flip_Flop d_ff_44 (.clk(m_1_out2[0]), .D(_35), .Q(_43));  // open: Qn, preset, en, reset
  D_Flip_Flop d_ff_45 (.clk(m_1_out2[0]), .D(_36), .Q(_44));  // open: Qn, preset, en, reset
  D_Flip_Flop d_ff_46 (.clk(m_1_out2[0]), .D(_37), .Q(_45));  // open: Qn, preset, en, reset
  D_Flip_Flop d_ff_47 (.clk(m_1_out2[0]), .D(_38), .Q(_46));  // open: Qn, preset, en, reset
  D_Flip_Flop d_ff_48 (.clk(m_1_out2[0]), .D(_39), .Q(_47));  // open: Qn, preset, en, reset
  D_Flip_Flop d_ff_49 (.clk(m_1_out2[0]), .D(_40), .Q(_48));  // open: Qn, preset, en, reset
  D_Flip_Flop d_ff_50 (.clk(m_1_out2[0]), .D(_41), .Q(_49));  // open: Qn, preset, en, reset
  D_Flip_Flop d_ff_51 (.clk(m_1_out2[0]), .D(_42), .Q(_50));  // open: Qn, preset, en, reset
  D_Flip_Flop d_ff_52 (.clk(m_1_out2[0]), .D(_43), .Q(_43));  // open: Qn, preset, en, reset
  D_Flip_Flop d_ff_53 (.clk(m_1_out2[0]), .D(_44), .Q(_52));  // open: Qn, preset, en, reset
  D_Flip_Flop d_ff_54 (.clk(m_1_out2[0]), .D(_45), .Q(_53));  // open: Qn, preset, en, reset
  D_Flip_Flop d_ff_55 (.clk(m_1_out2[0]), .D(_46), .Q(_54));  // open: Qn, preset, en, reset
  D_Flip_Flop d_ff_56 (.clk(m_1_out2[0]), .D(_47), .Q(_55));  // open: Qn, preset, en, reset
  D_Flip_Flop d_ff_57 (.clk(m_1_out2[0]), .D(_48), .Q(_56));  // open: Qn, preset, en, reset
  D_Flip_Flop d_ff_58 (.clk(m_1_out2[0]), .D(_49), .Q(_57));  // open: Qn, preset, en, reset
  D_Flip_Flop d_ff_59 (.clk(m_1_out2[0]), .D(_50), .Q(_58));  // open: Qn, preset, en, reset
  D_Flip_Flop d_ff_60 (.clk(m_1_out2[0]), .D(_43), .Q(_59));  // open: Qn, preset, en, reset
  D_Flip_Flop d_ff_61 (.clk(m_1_out2[0]), .D(_52), .Q(_60));  // open: Qn, preset, en, reset
  D_Flip_Flop d_ff_62 (.clk(m_1_out2[0]), .D(_53), .Q(_61));  // open: Qn, preset, en, reset
  D_Flip_Flop d_ff_63 (.clk(m_1_out2[0]), .D(_54), .Q(_62));  // open: Qn, preset, en, reset
  D_Flip_Flop d_ff_64 (.clk(m_1_out2[0]), .D(_55), .Q(_63));  // open: Qn, preset, en, reset

  // Other names for the same wires on the sheet: _51 = _43
endmodule

module M (
  input  Ativar_Clock,
  input  [7:0] In0,
  input  [7:0] In1,
  input  [7:0] In2,
  input  [7:0] In3,
  output [7:0] Out0,
  output [7:0] Out1,
  output [7:0] Out2,
  output [7:0] Out3
);

  wire _0, acr, acw, bw, c, clock, endw, fim, in, \Microinstrução_out , not_1_out, not_2_out, out, pc_1,
       pchr, pchw, pclr, pclw, \Proxima_Instrução_out , ramr, ramw, regR, regW, riw, romr, sp_1, sp_1_t,
       stackr, stackw, ular, z;
  wire [1:0] regop;
  wire [2:0] ulaop;
  wire [3:0] AC_saida_de_dados_controlada, AC_saida_de_dados_controlada_2, \AC_saída_de_dados_direta ,
       \AC_saída_de_dados_direta_2 , \Buf_saída_de_dados_direta , \Buf_saída_de_dados_direta_2 , End_p3,
       End_p3_2, \PC_saída_de_endereço_de_programa__rom_2 , \RI_saída_de_dados_direta ,
       \RI_saída_de_dados_direta_2 , \SP_saída_contador , \SP_saída_contador_2 ;
  wire [7:0] Registradores_b, Registradores_c, Registradores_d, Registradores_e;
  wire [15:0] \PC_saída_de_endereço_de_programa__rom ;

  Button \Proxima_Instrução  (.out(\Proxima_Instrução_out ));
  Button \Microinstrução  (.out(\Microinstrução_out ));
  Controle_do_Clock controle_do_clock_1 (
    .Ativar_Clock(Ativar_Clock), .\Proxima_Instrução (\Proxima_Instrução_out ),
    .\Microinstrução (\Microinstrução_out ), .\Fim_da_Instrução (fim), .\Saída_do_Clock (clock));
  Registrador RI (
    .Gravar(riw), .Reset(_0),
    .Entrada_de_Dados({AC_saida_de_dados_controlada_2, AC_saida_de_dados_controlada}),
    .\Saída_de_Dados_Direta ({\RI_saída_de_dados_direta_2 , \RI_saída_de_dados_direta }));
  Hex_Digit_Display hex_digit_display_1 (.value(\RI_saída_de_dados_direta ));  // open: dp
  Hex_Digit_Display hex_digit_display_2 (.value(\RI_saída_de_dados_direta_2 ));  // open: dp
  Unidade_de_Controle unidade_de_controle_1 (
    .Reset(_0), .Clock(clock), .\Operação_da_ULA (ulaop), .RI_W(riw), .AC_W(acw), .AC_R(acr), .PC_H_W(pchw),
    .SP_1(sp_1), .Buf_W(bw), .End_W(endw), .\Fim_da_Instrução (fim),
    .\Instrução__RI ({\RI_saída_de_dados_direta_2 , \RI_saída_de_dados_direta }), .Flag_Z(z), .Flag_C(c),
    .Registrador_ou_In_Out(regop), .ULA_R(ular), .Reg_W(regW), .Reg_R(regR), .In(in), .Out(out),
    .SP_1_2(sp_1_t), .PC_1(pc_1), .PC_H_R(pchr), .PC_L_R(pclr), .RAM_W(ramw), .RAM_R(ramr), .ROM_R(romr),
    .PC_L_W(pclw), .STACK_W(stackw), .STACK_R(stackr));
  Hex_Digit_Display hex_digit_display_3 (.value(\AC_saída_de_dados_direta ));  // open: dp
  Hex_Digit_Display hex_digit_display_4 (.value(\AC_saída_de_dados_direta_2 ));  // open: dp
  LED \Fim_da_Instrução  (.in(fim));
  Registrador_Acumulador AC (
    .Gravar(acw), .Ler(acr), .Reset(_0),
    .Entrada_de_Dados({AC_saida_de_dados_controlada_2, AC_saida_de_dados_controlada}),
    .Saida_de_Dados_Controlada({AC_saida_de_dados_controlada_2, AC_saida_de_dados_controlada}),
    .\Saída_de_Dados_Direta ({\AC_saída_de_dados_direta_2 , \AC_saída_de_dados_direta }));
  Hex_Digit_Display hex_digit_display_5 (.value(AC_saida_de_dados_controlada_2));  // open: dp
  Hex_Digit_Display hex_digit_display_6 (.value(AC_saida_de_dados_controlada));  // open: dp
  Hex_Digit_Display hex_digit_display_7 (.value(\Buf_saída_de_dados_direta ));  // open: dp
  Hex_Digit_Display hex_digit_display_8 (.value(\Buf_saída_de_dados_direta_2 ));  // open: dp
  ULA ULA (
    .Ler(ular), .\Operação (ulaop), .Reset(_0),
    .Operando_A({\AC_saída_de_dados_direta_2 , \AC_saída_de_dados_direta }),
    .Operando_B({\Buf_saída_de_dados_direta_2 , \Buf_saída_de_dados_direta }),
    .Resultado({AC_saida_de_dados_controlada_2, AC_saida_de_dados_controlada}), .Flag_C(c), .Flag_Z(z));
  Hex_Digit_Display hex_digit_display_9 (.value(AC_saida_de_dados_controlada_2));  // open: dp
  Hex_Digit_Display hex_digit_display_10 (.value(AC_saida_de_dados_controlada));  // open: dp
  Registrador Buf (
    .Gravar(bw), .Reset(_0),
    .Entrada_de_Dados({AC_saida_de_dados_controlada_2, AC_saida_de_dados_controlada}),
    .\Saída_de_Dados_Direta ({\Buf_saída_de_dados_direta_2 , \Buf_saída_de_dados_direta }));
  Hex_Digit_Display hex_digit_display_11 (.value(\SP_saída_contador_2 ));  // open: dp
  Banco_de_Registradores Registradores (
    .\Seleção (regop), .Gravar(regW), .Ler(regR),
    .Entrada_do_Barramento_de_Dados({AC_saida_de_dados_controlada_2, AC_saida_de_dados_controlada}),
    .\Saída_para_o_Barramento_de_Dados ({AC_saida_de_dados_controlada_2, AC_saida_de_dados_controlada}),
    .Reset(_0), .B(Registradores_b), .C(Registradores_c), .D(Registradores_d), .E(Registradores_e));
  Contador SP (
    .plus_1(sp_1), .minus_1(sp_1_t), .Reset(_0),
    .\Saída_Contador ({\SP_saída_contador_2 , \SP_saída_contador }));
  Hex_Digit_Display hex_digit_display_12 (.value(\SP_saída_contador ));  // open: dp
  // Probe on Registradores_b
  // Probe on Registradores_c
  // Probe on Registradores_d
  // Probe on Registradores_e
  not not_1 (not_1_out, stackw);
  \Portas_de_Entrada_e_Saída  \portas_de_entrada_e_saída_1  (
    .Ler(in), .\Seleção (regop), .Gravar(out), .Reset(_0),
    .\Saída_para_Barramento_de_Dados ({AC_saida_de_dados_controlada_2, AC_saida_de_dados_controlada}),
    .Entrada_do_Barramento_de_Dados({AC_saida_de_dados_controlada_2, AC_saida_de_dados_controlada}),
    .In0(In0), .Out0(Out0), .In1(In1), .In3(In3), .In2(In2), .Out0_2(Out1), .Out0_3(Out2), .Out0_4(Out3));
  RAM ram_1 (
    .addr({\SP_saída_contador_2 , \SP_saída_contador }),
    .data({AC_saida_de_dados_controlada_2, AC_saida_de_dados_controlada}), .clk(not_1_out), .ld(stackr),
    .clr(_0));  // open: sel
  Registrador_Program_Counter__16bits PC (
    .Incrementar__1(pc_1), .Gravar_PC_H(pchw), .Ler_PC_H(pchr), .Resetar(_0), .Gravar_PC_L(pclw),
    .Ler_PC_L(pclr),
    .Entrada_do_Barramento_de_Dados({AC_saida_de_dados_controlada_2, AC_saida_de_dados_controlada}),
    .Saida_para_o_Barramento_de_Dados({AC_saida_de_dados_controlada_2, AC_saida_de_dados_controlada}),
    .\Saída_de_Endereço_de_Programa__ROM ({\PC_saída_de_endereço_de_programa__rom [15:12], \PC_saída_de_endereço_de_programa__rom_2 , \PC_saída_de_endereço_de_programa__rom [7:0]}));
  Hex_Digit_Display hex_digit_display_13 (.value(\PC_saída_de_endereço_de_programa__rom [15:12]));  // open: dp
  Hex_Digit_Display hex_digit_display_14 (.value(\PC_saída_de_endereço_de_programa__rom_2 ));  // open: dp
  Hex_Digit_Display hex_digit_display_15 (.value(End_p3_2));  // open: dp
  Hex_Digit_Display hex_digit_display_16 (.value(\PC_saída_de_endereço_de_programa__rom [3:0]));  // open: dp
  Hex_Digit_Display hex_digit_display_17 (.value(\PC_saída_de_endereço_de_programa__rom [7:4]));  // open: dp
  // Registrador End: pin names not known; wires that end beside it: endw, {AC_saida_de_dados_controlada_2, AC_saida_de_dados_controlada}, {End_p3_2, End_p3}, _0
  Hex_Digit_Display hex_digit_display_18 (.value(End_p3));  // open: dp
  Button Reset (.out(_0));
  not not_2 (not_2_out, ramw);
  ROM #(.addrWidth(16)) rom_1 (
    .addr({\PC_saída_de_endereço_de_programa__rom [15:12], \PC_saída_de_endereço_de_programa__rom_2 , \PC_saída_de_endereço_de_programa__rom [7:0]}),
    .data({AC_saida_de_dados_controlada_2, AC_saida_de_dados_controlada}), .sel(romr));
  RAM ram_2 (
    .addr({End_p3_2, End_p3}), .data({AC_saida_de_dados_controlada_2, AC_saida_de_dados_controlada}),
    .clk(not_2_out), .ld(ramr), .clr(_0));  // open: sel

  // Notes on the sheet:
  //   Barramento de Dados
  //   Memória de Pilha
  //   Portas In/Out
  //   Memória de Programa
  //   Memória de Dados
  //   contents of rom_1 (hex, n*v repeats v):
  //   de 7 20 3 7 5 0 c 7 3 0 cc 7 c0 1 db 7 6 2 d4 7 c0 1 db 7 6 2 d4 7 c0 ff db 7 6 2 d4 7 c0 1 db 7 6 2
  //   d4 7 c0 1 db 7 6 2 d4 7 c0 0 db 7 6 2 d4 7 c0 ff db 7 6 2 d4 7 c0 19 db 7 6 2 d4 7 c0 29 db 7 6 2 d4
  //   7 c0 49 db 7 6 2 d4 7 c0 86 db 7 6 2 d4 7 c0 0 db 7 6 2 d4 7 c0 ff db 7 6 2 d4 7 c0 91 db 7 6 2 d4 7
  //   c0 91 db 7 6 2 d4 7 c0 91 db 7 6 2 d4 7 c0 91 db 7 6 2 d4 7 c0 0 db 7 6 2 d4 7 c0 9f db 7 6 2 d4 7
  //   c0 91 db 7 6 2 d4 7 c0 91 db 7 6 2 d4 7 c0 91 db 7 6 2 d4 7 c0 f1 db 7 6 2 d4 7 c0 0 db 7 6 2 d4 de
  //   7 20 2 7 5 0 d8 7 3 1 98 7 c0 ff db 7 6 2 d4 7 c0 81 db 7 6 2 d4 7 c0 81 db 7 6 2 d4 7 c0 42 db 7 6
  //   2 d4 7 c0 3c db 7 6 2 d4 7 c0 0 db 7 6 2 d4 7 c0 7e db 7 6 2 d4 7 c0 81 db 7 6 2 d4 7 c0 81 db 7 6 2
  //   d4 7 c0 81 db 7 6 2 d4 7 c0 7e db 7 6 2 d4 7 c0 0 db 7 6 2 d4 7 c0 0 db 7 6 2 d4 7 c0 81 db 7 6 2 d4
  //   7 c0 ff db 7 6 2 d4 7 c0 81 db 7 6 2 d4 7 c0 0 db 7 6 2 d4 7 c0 0 db 7 6 2 d4 7 c0 9f db 7 6 2 d4 7
  //   c0 91 db 7 6 2 d4 7 c0 91 db 7 6 2 d4 7 c0 91 db 7 6 2 d4 7 c0 f1 db 7 6 2 d4 7 c0 0 db 7 6 2 d4 de
  //   7 20 1 7 5 1 a4 7 3 2 4 7 c0 ff db 7 6 2 d4 7 c0 80 db 7 6 2 d4 7 c0 80 db 7 6 2 d4 7 c0 80 db 7 6 2
  //   d4 7 c0 7f db 7 6 2 d4 7 c0 0 db 7 6 2 d4 7 c0 ff db 7 6 2 d4 7 c0 6 db 7 6 2 d4 7 c0 c db 7 6 2 d4
  //   7 c0 6 db 7 6 2 d4 7 c0 ff db 7 6 2 d4 7 c0 0 db 7 6 2 d4 de 7 20 0 7 5 2 10 7 3 2 d0 7 c0 c1 db 7 6
  //   2 d4 7 c0 a1 db 7 6 2 d4 7 c0 99 db 7 6 2 d4 7 c0 85 db 7 6 2 d4 7 c0 83 db 7 6 2 d4 7 c0 0 db 7 6 2
  //   d4 7 c0 ff db 7 6 2 d4 7 c0 91 db 7 6 2 d4 7 c0 91 db 7 6 2 d4 7 c0 91 db 7 6 2 d4 7 c0 91 db 7 6 2
  //   d4 7 c0 0 db 7 6 2 d4 7 c0 ff db 7 6 2 d4 7 c0 19 db 7 6 2 d4 7 c0 29 db 7 6 2 d4 7 c0 49 db 7 6 2
  //   d4 7 c0 86 db 7 6 2 d4 7 c0 0 db 7 6 2 d4 7 c0 7e db 7 6 2 d4 7 c0 81 db 7 6 2 d4 7 c0 81 db 7 6 2
  //   d4 7 c0 81 db 7 6 2 d4 7 c0 7e db 7 6 2 d4 7 c0 0 db 7 6 2 d4 7 3 2 d0 7 c0 0 d3 7 c0 1 d3 7 c0 0 d3
  //   7 7
endmodule

module Unidade_de_Controle (
  input  [7:0] \Instrução__RI ,
  input  Reset,
  input  Flag_C,
  input  Flag_Z,
  input  Clock,
  output [2:0] \Operação_da_ULA ,
  output RI_W,
  output [1:0] Registrador_ou_In_Out,
  output AC_W,
  output AC_R,
  output Buf_W,
  output ULA_R,
  output Reg_W,
  output Reg_R,
  output In,
  output Out,
  output SP_1,
  output SP_1_2,
  output End_W,
  output PC_1,
  output PC_H_R,
  output PC_H_W,
  output PC_L_R,
  output PC_L_W,
  output STACK_W,
  output STACK_R,
  output \Fim_da_Instrução ,
  output RAM_W,
  output RAM_R,
  output ROM_R
);

  wire and_1_out, and_2_out, and_3_out, and_4_out, buffer_1_out, buffer_2_out, buffer_4_out, buffer_5_out,
       Higth_Decoder, IC_0, IC_W, not_1_out, or_1_out, or_2_out, or_3_out;
  wire [4:3] counter_1_q;
  wire [7:0] IC_saida_de_dados, rom_1_data;
  wire [30:16] multiplexer_1_out;
  wire [31:0] rom_2_data;

  or or_1 (or_1_out, IC_0, Reset);
  Counter #(.width(2), .max('h3)) counter_1 (
    .Q(counter_1_q), .clk(Higth_Decoder), .clr(or_1_out));  // open: load, D, count, carry
  not not_1 (not_1_out, IC_W);
  or or_2 (or_2_out, IC_saida_de_dados[0], IC_saida_de_dados[1], IC_saida_de_dados[2], IC_saida_de_dados[3], IC_saida_de_dados[4], IC_saida_de_dados[5], IC_saida_de_dados[6], IC_saida_de_dados[7]);
  not not_2 (\Fim_da_Instrução , or_2_out);
  ROM #(.addrWidth(5)) rom_1 (.addr({counter_1_q, \Instrução__RI [2:0]}), .data(rom_1_data));  // open: sel
  Registrador_Program_Counter IC (
    .Incrementar__1(Clock), .Gravar(not_1_out), .Resetar(or_3_out), .Entrada_de_Dados(rom_1_data),
    .Saida_de_Dados(IC_saida_de_dados));  // open: Estouro
  or or_3 (or_3_out, Reset, IC_0);
  ROM #(.dataWidth(32)) rom_2 (.addr(IC_saida_de_dados), .data(rom_2_data));  // open: sel
  Multiplexer #(.width(32)) multiplexer_1 (
    .in0({32{1'b0}}), .in1(rom_2_data),
    .out({Higth_Decoder, multiplexer_1_out[30:28], ROM_R, multiplexer_1_out[26], RAM_W, multiplexer_1_out[24], STACK_W, multiplexer_1_out[22:20], PC_L_R, multiplexer_1_out[18:16], PC_H_R, PC_1, End_W, SP_1_2, SP_1, Out, In, Reg_R, Reg_W, ULA_R, Buf_W, AC_R, AC_W, RI_W, IC_W, IC_0}),
    .sel(Clock));  // open: en
  buf buffer_1 (buffer_1_out, multiplexer_1_out[24]);
  buf buffer_2 (buffer_2_out, buffer_1_out);
  buf buffer_3 (STACK_R, buffer_2_out);
  buf buffer_4 (buffer_4_out, multiplexer_1_out[26]);
  buf buffer_5 (buffer_5_out, buffer_4_out);
  buf buffer_6 (RAM_R, buffer_5_out);
  and and_1 (and_1_out, Flag_C, multiplexer_1_out[17]);
  and and_2 (and_2_out, Flag_C, multiplexer_1_out[21]);
  or or_4 (PC_H_W, multiplexer_1_out[16], and_1_out, and_3_out);
  and and_3 (and_3_out, Flag_Z, multiplexer_1_out[18]);
  or or_5 (PC_L_W, multiplexer_1_out[20], and_2_out, and_4_out);
  and and_4 (and_4_out, Flag_Z, multiplexer_1_out[22]);

  assign \Operação_da_ULA  = \Instrução__RI [7:5];
  assign Registrador_ou_In_Out = \Instrução__RI [4:3];

  // Notes on the sheet:
  //   Decodificador de Instrução
  //   contents of rom_1 (hex, n*v repeats v):
  //   3 6 9 d 10 13 17 1a 1d 20 23 27 2b 30 35 3b 3e 43 47 4b 4d 4f 51 53
  //   Memória de Controle
  //   contents of rom_2 (hex, n*v repeats v):
  //   8004004 2 0 30 49 0 30 c1 0 8006000 30 2000041 0 30 441 0 120 49 0 8006000 4000020 49 0 220 49 0
  //   88004004 2 0 8004020 49 0 8004020 c1 0 8004020 8006000 2000041 0 8805000 8100000 1010801 0 8805000
  //   8805000 1200800 1020801 0 8805000 8805000 1400800 1040801 0 809000 881000 8805000 8100000 1010801 0
  //   88004004 2 0 1100800 1010800 4000 4001 0 2100 4000020 49 0 2100 30 2000041 0 801101 0 1000881 0
  //   801011 0 1000809 0 1
  //   PC-H-W
  //   PC-H-W-C
  //   PC-H-W-Z
  //   PC-L-W
  //   PC-L-W-C
  //   PC-L-W-Z
endmodule

module ULA (
  input  [7:0] Operando_A,
  input  [7:0] Operando_B,
  input  Ler,
  input  [2:0] \Operação ,
  input  Reset,
  output Flag_C,
  output Flag_Z,
  output [7:0] Resultado
);

  wire adder_1_cout, and_2_out, and_3_out, and_4_out, demultiplexer_1_out0, demultiplexer_1_out1,
       demultiplexer_1_out2, demultiplexer_1_out3, demultiplexer_1_out4, demultiplexer_1_out5,
       demultiplexer_1_out6, demultiplexer_1_out7, incremento_1_1_estouro__carry, not_2_out, or_2_out,
       or_3_out, subtractor_1_bout;
  wire [7:0] adder_1_out, and_1_out, \incremento_1_1_saída , not_1_out, or_1_out, subtractor_1_out, xor_1_out;

  Demultiplexer #(.select(3)) demultiplexer_1 (
    .out0(demultiplexer_1_out0), .out1(demultiplexer_1_out1), .out2(demultiplexer_1_out2),
    .out3(demultiplexer_1_out3), .out4(demultiplexer_1_out4), .out5(demultiplexer_1_out5),
    .out6(demultiplexer_1_out6), .out7(demultiplexer_1_out7), .in(Ler), .sel(\Operação ));  // open: en
  Adder adder_1 (.a(Operando_A), .b(Operando_B), .out(adder_1_out), .cout(adder_1_cout));  // open: cin
  assign Resultado = demultiplexer_1_out0 ? adder_1_out : 8'bz;  // Controlled_Buffer controlled_buffer_1
  Subtractor subtractor_1 (
    .a(Operando_A), .b(Operando_B), .out(subtractor_1_out), .bout(subtractor_1_bout));  // open: bin
  assign Resultado = demultiplexer_1_out1 ? subtractor_1_out : 8'bz;  // Controlled_Buffer controlled_buffer_2
  assign and_1_out = Operando_A & Operando_B;  // AND_Gate and_1, 8 bits wide
  assign Resultado = demultiplexer_1_out2 ? and_1_out : 8'bz;  // Controlled_Buffer controlled_buffer_3
  assign or_1_out = Operando_A | Operando_B;  // OR_Gate or_1, 8 bits wide
  assign Resultado = demultiplexer_1_out3 ? or_1_out : 8'bz;  // Controlled_Buffer controlled_buffer_4
  assign xor_1_out = Operando_A ^ Operando_B;  // XOR_Gate xor_1, 8 bits wide
  assign Resultado = demultiplexer_1_out4 ? xor_1_out : 8'bz;  // Controlled_Buffer controlled_buffer_5
  assign not_1_out = ~Operando_B;  // NOT_Gate not_1, 8 bits wide
  assign Resultado = demultiplexer_1_out5 ? not_1_out : 8'bz;  // Controlled_Buffer controlled_buffer_6
  assign Resultado = demultiplexer_1_out6 ? Operando_B : 8'bz;  // Controlled_Buffer controlled_buffer_7
  Incremento__1 incremento_1_1 (
    .\Saída (\incremento_1_1_saída ), .Estouro__Carry(incremento_1_1_estouro__carry), .Entrada(Operando_B));
  assign Resultado = demultiplexer_1_out7 ? \incremento_1_1_saída  : 8'bz;  // Controlled_Buffer controlled_buffer_8
  and and_2 (and_2_out, adder_1_cout, demultiplexer_1_out0);
  and and_3 (and_3_out, subtractor_1_bout, demultiplexer_1_out1);
  or or_2 (or_2_out, and_2_out, and_3_out, and_4_out);
  and and_4 (and_4_out, incremento_1_1_estouro__carry, demultiplexer_1_out7);
  or or_3 (or_3_out, Resultado[0], Resultado[1], Resultado[2], Resultado[3], Resultado[4], Resultado[5], Resultado[6], Resultado[7]);
  D_Flip_Flop #(.trigger("falling")) d_ff_1 (
    .clk(Ler), .D(or_2_out), .Q(Flag_C), .reset(Reset));  // open: Qn, preset, en
  D_Flip_Flop #(.trigger("falling")) d_ff_2 (
    .clk(Ler), .D(not_2_out), .Q(Flag_Z), .reset(Reset));  // open: Qn, preset, en
  not not_2 (not_2_out, or_3_out);

  // Notes on the sheet:
  //   SUB
  //   ADD
  //   AND
  //   OR
  //   XOR
  //   NOT
  //   Bypass
  //   Inc+1
endmodule

module Banco_de_Registradores (
  input  [7:0] Entrada_do_Barramento_de_Dados,
  input  Gravar,
  input  [1:0] \Seleção ,
  input  Ler,
  input  Reset,
  output [7:0] B,
  output [7:0] C,
  output [7:0] D,
  output [7:0] E,
  output [7:0] \Saída_para_o_Barramento_de_Dados 
);

  wire and_1_out, and_2_out, and_3_out, and_4_out, and_5_out, and_6_out, and_7_out, and_8_out,
       decoder_1_out0, decoder_1_out1, decoder_1_out2, decoder_1_out3;

  Register #(.trigger("falling")) u_B (
    .D(Entrada_do_Barramento_de_Dados), .Q(B), .clk(and_1_out), .clr(Reset));  // open: en
  and and_1 (and_1_out, decoder_1_out0, Gravar);
  Register #(.trigger("falling")) u_C (
    .D(Entrada_do_Barramento_de_Dados), .Q(C), .clk(and_2_out), .clr(Reset));  // open: en
  and and_2 (and_2_out, decoder_1_out1, Gravar);
  Register #(.trigger("falling")) u_D (
    .D(Entrada_do_Barramento_de_Dados), .Q(D), .clk(and_3_out), .clr(Reset));  // open: en
  and and_3 (and_3_out, decoder_1_out2, Gravar);
  Register #(.trigger("falling")) u_E (
    .D(Entrada_do_Barramento_de_Dados), .Q(E), .clk(and_4_out), .clr(Reset));  // open: en
  and and_4 (and_4_out, decoder_1_out3, Gravar);
  Decoder #(.select(2)) decoder_1 (
    .out0(decoder_1_out0), .out1(decoder_1_out1), .out2(decoder_1_out2), .out3(decoder_1_out3),
    .sel(\Seleção ));  // open: en
  assign \Saída_para_o_Barramento_de_Dados  = and_5_out ? B : 8'bz;  // Controlled_Buffer controlled_buffer_1
  and and_5 (and_5_out, decoder_1_out0, Ler);
  assign \Saída_para_o_Barramento_de_Dados  = and_6_out ? C : 8'bz;  // Controlled_Buffer controlled_buffer_2
  and and_6 (and_6_out, decoder_1_out1, Ler);
  assign \Saída_para_o_Barramento_de_Dados  = and_7_out ? D : 8'bz;  // Controlled_Buffer controlled_buffer_3
  and and_7 (and_7_out, decoder_1_out2, Ler);
  assign \Saída_para_o_Barramento_de_Dados  = and_8_out ? E : 8'bz;  // Controlled_Buffer controlled_buffer_4
  and and_8 (and_8_out, decoder_1_out3, Ler);
endmodule

module \Portas_de_Entrada_e_Saída  (
  input  [1:0] \Seleção ,
  input  Ler,
  input  Gravar,
  input  Reset,
  input  [7:0] In0,
  input  [7:0] In1,
  input  [7:0] In2,
  input  [7:0] In3,
  input  [7:0] Entrada_do_Barramento_de_Dados,
  output [7:0] Out0,
  output [7:0] Out0_2,
  output [7:0] Out0_3,
  output [7:0] Out0_4,
  output [7:0] \Saída_para_Barramento_de_Dados 
);

  wire and_1_out, and_2_out, and_3_out, and_4_out, and_5_out, and_6_out, and_7_out, and_8_out,
       decoder_1_out0, decoder_1_out1, decoder_1_out2, decoder_1_out3;

  assign \Saída_para_Barramento_de_Dados  = and_1_out ? In0 : 8'bz;  // Controlled_Buffer controlled_buffer_1
  assign \Saída_para_Barramento_de_Dados  = and_2_out ? In1 : 8'bz;  // Controlled_Buffer controlled_buffer_2
  assign \Saída_para_Barramento_de_Dados  = and_3_out ? In2 : 8'bz;  // Controlled_Buffer controlled_buffer_3
  assign \Saída_para_Barramento_de_Dados  = and_4_out ? In3 : 8'bz;  // Controlled_Buffer controlled_buffer_4
  and and_1 (and_1_out, decoder_1_out0, Ler);
  and and_2 (and_2_out, decoder_1_out1, Ler);
  and and_3 (and_3_out, decoder_1_out2, Ler);
  and and_4 (and_4_out, decoder_1_out3, Ler);
  Decoder #(.select(2)) decoder_1 (
    .out0(decoder_1_out0), .out1(decoder_1_out1), .out2(decoder_1_out2), .out3(decoder_1_out3),
    .sel(\Seleção ));  // open: en
  and and_5 (and_5_out, decoder_1_out0, Gravar);
  and and_6 (and_6_out, decoder_1_out1, Gravar);
  and and_7 (and_7_out, decoder_1_out2, Gravar);
  and and_8 (and_8_out, decoder_1_out3, Gravar);
  Register #(.trigger("falling")) register_1 (
    .D(Entrada_do_Barramento_de_Dados), .Q(Out0), .clk(and_5_out), .clr(Reset));  // open: en
  Register #(.trigger("falling")) register_2 (
    .D(Entrada_do_Barramento_de_Dados), .Q(Out0_2), .clk(and_6_out), .clr(Reset));  // open: en
  Register #(.trigger("falling")) register_3 (
    .D(Entrada_do_Barramento_de_Dados), .Q(Out0_3), .clk(and_7_out), .clr(Reset));  // open: en
  Register #(.trigger("falling")) register_4 (
    .D(Entrada_do_Barramento_de_Dados), .Q(Out0_4), .clk(and_8_out), .clr(Reset));  // open: en
endmodule

module Registrador (
  input  [7:0] Entrada_de_Dados,
  input  Gravar,
  input  Reset,
  output [7:0] \Saída_de_Dados_Direta 
);

  Register #(.trigger("falling")) register_1 (
    .D(Entrada_de_Dados), .Q(\Saída_de_Dados_Direta ), .clk(Gravar), .clr(Reset));  // open: en
endmodule

module Registrador_Acumulador (
  input  [7:0] Entrada_de_Dados,
  input  Gravar,
  input  Ler,
  input  Reset,
  output [7:0] Saida_de_Dados_Controlada,
  output [7:0] \Saída_de_Dados_Direta 
);

  Register #(.trigger("falling")) register_1 (
    .D(Entrada_de_Dados), .Q(\Saída_de_Dados_Direta ), .clk(Gravar), .clr(Reset));  // open: en
  assign Saida_de_Dados_Controlada = Ler ? \Saída_de_Dados_Direta  : 8'bz;  // Controlled_Buffer controlled_buffer_1
endmodule

module Registrador_Program_Counter (
  input  [7:0] Entrada_de_Dados,
  input  Incrementar__1,
  input  Gravar,
  input  Resetar,
  output Estouro,
  output [7:0] Saida_de_Dados
);

  wire d_ff_1_q, d_ff_2_q, d_ff_3_q, incremento_1_1_estouro__carry, not_1_out, or_1_out;
  wire [7:0] \incremento_1_1_saída , multiplexer_1_out;

  D_Flip_Flop #(.trigger("falling")) d_ff_1 (
    .clk(Incrementar__1), .D(1'b1), .Q(d_ff_1_q), .reset(d_ff_1_q));  // open: Qn, preset, en
  D_Flip_Flop #(.trigger("falling")) d_ff_2 (
    .clk(Gravar), .D(1'b1), .Q(d_ff_2_q), .reset(d_ff_2_q));  // open: Qn, preset, en
  D_Flip_Flop #(.trigger("falling")) d_ff_3 (
    .clk(Resetar), .D(1'b1), .Q(d_ff_3_q), .reset(d_ff_3_q));  // open: Qn, preset, en
  Incremento__1 incremento_1_1 (
    .\Saída (\incremento_1_1_saída ), .Estouro__Carry(incremento_1_1_estouro__carry), .Entrada(Saida_de_Dados));
  Multiplexer #(.width(8)) multiplexer_1 (
    .in0(\incremento_1_1_saída ), .in1(Entrada_de_Dados), .out(multiplexer_1_out), .sel(not_1_out));  // open: en
  not not_1 (not_1_out, d_ff_1_q);
  and and_1 (Estouro, incremento_1_1_estouro__carry, Incrementar__1);
  or or_1 (or_1_out, d_ff_1_q, d_ff_2_q);
  Register #(.trigger("falling")) register_1 (
    .D(multiplexer_1_out), .Q(Saida_de_Dados), .clk(or_1_out), .clr(d_ff_3_q));  // open: en
endmodule

module Registrador_Program_Counter__16bits (
  input  [7:0] Entrada_do_Barramento_de_Dados,
  input  Incrementar__1,
  input  Resetar,
  input  Gravar_PC_H,
  input  Gravar_PC_L,
  input  Ler_PC_H,
  input  Ler_PC_L,
  output [7:0] Saida_para_o_Barramento_de_Dados,
  output [15:0] \Saída_de_Endereço_de_Programa__ROM 
);

  wire PC__L_estouro;

  S_R_Flip_Flop s_r_ff_1 (.preset(Incrementar__1));  // open: S, clk, R, Q, Qn, reset, en
  S_R_Flip_Flop s_r_ff_2 (.preset(Gravar_PC_H));  // open: S, clk, R, Q, Qn, reset, en
  S_R_Flip_Flop s_r_ff_3 (.preset(Ler_PC_H));  // open: S, clk, R, Q, Qn, reset, en
  Registrador_Program_Counter PC__H (
    .Incrementar__1(PC__L_estouro), .Gravar(Gravar_PC_H), .Resetar(Resetar),
    .Entrada_de_Dados(Entrada_do_Barramento_de_Dados),
    .Saida_de_Dados(\Saída_de_Endereço_de_Programa__ROM [15:8]));  // open: Estouro
  assign Saida_para_o_Barramento_de_Dados = Ler_PC_H ? \Saída_de_Endereço_de_Programa__ROM [15:8] : 8'bz;  // Controlled_Buffer controlled_buffer_1
  Registrador_Program_Counter PC__L (
    .Incrementar__1(Incrementar__1), .Gravar(Gravar_PC_L), .Resetar(Resetar), .Estouro(PC__L_estouro),
    .Entrada_de_Dados(Entrada_do_Barramento_de_Dados),
    .Saida_de_Dados(\Saída_de_Endereço_de_Programa__ROM [7:0]));
  assign Saida_para_o_Barramento_de_Dados = Ler_PC_L ? \Saída_de_Endereço_de_Programa__ROM [7:0] : 8'bz;  // Controlled_Buffer controlled_buffer_2
  S_R_Flip_Flop s_r_ff_4 (.preset(Resetar));  // open: S, clk, R, Q, Qn, reset, en
  S_R_Flip_Flop s_r_ff_5 (.preset(Gravar_PC_L));  // open: S, clk, R, Q, Qn, reset, en
  S_R_Flip_Flop s_r_ff_6 (.preset(Ler_PC_L));  // open: S, clk, R, Q, Qn, reset, en
endmodule

module Contador (
  input  plus_1,
  input  minus_1,
  input  Reset,
  output [7:0] \Saída_Contador 
);

  wire and_1_out, and_2_out, and_3_out, and_4_out, and_5_out, and_6_out, and_7_out, and_8_out, and_9_out,
       and_10_out, and_11_out, and_12_out, and_13_out, and_14_out, d_ff_1_q, j_k_ff_1_qn, j_k_ff_2_qn,
       j_k_ff_3_qn, j_k_ff_4_qn, j_k_ff_5_qn, j_k_ff_6_qn, j_k_ff_7_qn, or_1_out, or_2_out, or_3_out,
       or_4_out, or_5_out, or_6_out, or_7_out, or_8_out, undriven, undriven_2, undriven_3, undriven_4,
       undriven_5, undriven_6, undriven_7;

  D_Flip_Flop d_ff_1 (.clk(minus_1), .D(1'b1), .Q(d_ff_1_q), .reset(d_ff_1_q));  // open: Qn, preset, en
  J_K_Flip_Flop #(.trigger("falling")) j_k_ff_1 (
    .J(1'b1), .clk(or_1_out), .K(1'b1), .Q(\Saída_Contador [0]), .Qn(j_k_ff_1_qn), .reset(Reset));  // open: preset, en
  or or_1 (or_1_out, plus_1, d_ff_1_q);
  and and_1 (and_1_out, plus_1, \Saída_Contador [0]);
  and and_2 (and_2_out, j_k_ff_1_qn, d_ff_1_q);
  J_K_Flip_Flop #(.trigger("falling")) j_k_ff_2 (
    .J(1'b1), .clk(or_2_out), .K(1'b1), .Q(\Saída_Contador [1]), .Qn(j_k_ff_2_qn), .preset(undriven),
    .en(undriven), .reset(Reset));
  or or_2 (or_2_out, and_1_out, and_2_out);
  and and_3 (and_3_out, and_1_out, \Saída_Contador [1]);
  and and_4 (and_4_out, j_k_ff_2_qn, and_2_out);
  or or_3 (or_3_out, and_3_out, and_4_out);
  and and_5 (and_5_out, and_3_out, \Saída_Contador [2]);
  J_K_Flip_Flop #(.trigger("falling")) j_k_ff_3 (
    .J(1'b1), .clk(or_3_out), .K(1'b1), .Q(\Saída_Contador [2]), .Qn(j_k_ff_3_qn), .preset(undriven_2),
    .en(undriven_2), .reset(Reset));
  and and_6 (and_6_out, j_k_ff_3_qn, and_4_out);
  or or_4 (or_4_out, and_5_out, and_6_out);
  and and_7 (and_7_out, and_5_out, \Saída_Contador [3]);
  J_K_Flip_Flop #(.trigger("falling")) j_k_ff_4 (
    .J(1'b1), .clk(or_4_out), .K(1'b1), .Q(\Saída_Contador [3]), .Qn(j_k_ff_4_qn), .preset(undriven_3),
    .en(undriven_3), .reset(Reset));
  and and_8 (and_8_out, j_k_ff_4_qn, and_6_out);
  or or_5 (or_5_out, and_7_out, and_8_out);
  and and_9 (and_9_out, and_7_out, \Saída_Contador [4]);
  J_K_Flip_Flop #(.trigger("falling")) j_k_ff_5 (
    .J(1'b1), .clk(or_5_out), .K(1'b1), .Q(\Saída_Contador [4]), .Qn(j_k_ff_5_qn), .preset(undriven_4),
    .en(undriven_4), .reset(Reset));
  and and_10 (and_10_out, j_k_ff_5_qn, and_8_out);
  or or_6 (or_6_out, and_9_out, and_10_out);
  J_K_Flip_Flop #(.trigger("falling")) j_k_ff_6 (
    .J(1'b1), .clk(or_6_out), .K(1'b1), .Q(\Saída_Contador [5]), .Qn(j_k_ff_6_qn), .preset(undriven_5),
    .en(undriven_5), .reset(Reset));
  and and_11 (and_11_out, and_9_out, \Saída_Contador [5]);
  or or_7 (or_7_out, and_11_out, and_12_out);
  and and_12 (and_12_out, j_k_ff_6_qn, and_10_out);
  J_K_Flip_Flop #(.trigger("falling")) j_k_ff_7 (
    .J(1'b1), .clk(or_7_out), .K(1'b1), .Q(\Saída_Contador [6]), .Qn(j_k_ff_7_qn), .preset(undriven_6),
    .en(undriven_6), .reset(Reset));
  and and_13 (and_13_out, and_11_out, \Saída_Contador [6]);
  or or_8 (or_8_out, and_13_out, and_14_out);
  and and_14 (and_14_out, j_k_ff_7_qn, and_12_out);
  J_K_Flip_Flop #(.trigger("falling")) j_k_ff_8 (
    .J(1'b1), .clk(or_8_out), .K(1'b1), .Q(\Saída_Contador [7]), .preset(undriven_7), .en(undriven_7),
    .reset(Reset));  // open: Qn
endmodule

module Incremento__1 (
  input  [7:0] Entrada,
  output [7:0] \Saída ,
  output Estouro__Carry
);

  Adder adder_1 (.a(Entrada), .b(8'h1), .out(\Saída ), .cout(Estouro__Carry));  // open: cin
endmodule

module Controle_do_Clock (
  input  Ativar_Clock,
  input  \Proxima_Instrução ,
  input  \Microinstrução ,
  input  \Fim_da_Instrução ,
  output \Saída_do_Clock 
);

  wire and_1_out, and_2_out, Clock_out, d_ff_1_q, d_ff_2_q, s_r_ff_1_q;

  Clock Clock (.out(Clock_out));
  D_Flip_Flop d_ff_1 (.clk(\Proxima_Instrução ), .D(1'b1), .Q(d_ff_1_q), .reset(d_ff_1_q));  // open: Qn, preset, en
  D_Flip_Flop d_ff_2 (.clk(\Fim_da_Instrução ), .D(1'b1), .Q(d_ff_2_q), .reset(d_ff_2_q));  // open: Qn, preset, en
  and and_1 (and_1_out, Clock_out, Ativar_Clock);
  and and_2 (and_2_out, Clock_out, s_r_ff_1_q);
  S_R_Flip_Flop s_r_ff_1 (.Q(s_r_ff_1_q), .preset(d_ff_1_q), .reset(d_ff_2_q));  // open: S, clk, R, Qn, en
  or or_1 (\Saída_do_Clock , and_1_out, and_2_out, \Microinstrução );
endmodule
